// Logisim project computer-ascii.circ as structural Verilog: 6 circuits, main circuit main
module main (
);

  wire AD_L, adder_1_cout, ALU, buffer_1_out, button_1_out, button_2_out, button_3_out, button_4_out,
       clock_1_out, clock_2_out, controlled_buffer_2_out, controlled_buffer_3_out, controlled_buffer_4_out,
       controlled_buffer_7_out, counter_2_q, counter_4_q, demultiplexer_1_out0, demultiplexer_1_out1, HLT,
       IR, MCR, MIN, MO, n8_bit_or_1_output, n8_bit_or_2_output, n8_bit_or_3_output, n8_bit_or_4_output,
       n8_bit_or_5_output, not_1_out, not_2_out, not_3_out, not_4_out, not_5_out, not_7_out, not_8_out,
       not_9_out, not_10_out, or_3_out, or_5_out, or_7_out, OUT, PI, PL, PO, PROG, pull_resistor_17_node,
       pull_resistor_18_node, pull_resistor_20_node, pull_resistor_21_node, pull_resistor_23_node, RAIN,
       RAM_LOAD, RAOUT, RBIN, RL, SUB;
  wire [1:0] counter_3_q;
  wire [2:0] counter_1_q, pull_resistor_1_node;
  wire [3:0] or_6_out, register_5_q;
  wire [3:1] pull_resistor_24_node;
  wire [7:0] _3_out, adder_1_out, B_out, controlled_buffer_6_out, controlled_buffer_11_out,
       demultiplexer_2_out0, demultiplexer_2_out1, demultiplexer_2_out2, inv_1_output, LD_DATA, MAR_q, PC_q,
       RA_q, ram_1_data, RB, register_3_q, register_4_q, register_6_q, register_7_q, rom_2_data, ROUT;
  wire [7:5] IR_q;
  wire [10:5] pull_resistor_2_node;
  wire [15:0] rom_1_data;
  wire [15:5] controlled_buffer_1_out;

  not not_1 (not_1_out, MCR);
  Pull_Resistor pull_resistor_1 (.node(pull_resistor_1_node));
  Pull_Resistor pull_resistor_2 (.node(pull_resistor_2_node[10]));
  Counter #(.width(3), .max('h7)) counter_1 (
    .load(MCR), .D(pull_resistor_1_node), .count(not_1_out), .Q(counter_1_q), .clk(not_2_out),
    .clr(controlled_buffer_3_out));  // open: carry
  assign {controlled_buffer_1_out[15], SUB, RAM_LOAD, HLT, controlled_buffer_1_out[11], ALU, RBIN, RAOUT, RAIN, IR, controlled_buffer_1_out[5], MIN, PL, OUT, MO, PI} = PROG ? rom_1_data : 16'bz;  // Controlled_Buffer controlled_buffer_1
  ROM #(.addrWidth(11), .dataWidth(16)) rom_1 (
    .addr({pull_resistor_2_node, counter_1_q, register_5_q[3:2]}), .data(rom_1_data));  // open: sel
  Pull_Resistor pull_resistor_3 (.node(PI));
  Pull_Resistor pull_resistor_4 (.node(MO));
  Pull_Resistor pull_resistor_5 (.node(OUT));
  Pull_Resistor pull_resistor_6 (.node(PL));
  Pull_Resistor pull_resistor_7 (.node(MIN));
  Pull_Resistor pull_resistor_8 (.node(IR));
  Pull_Resistor pull_resistor_9 (.node(RAIN));
  Pull_Resistor pull_resistor_10 (.node(RAOUT));
  Pull_Resistor pull_resistor_11 (.node(RBIN));
  Pull_Resistor pull_resistor_12 (.node(ALU));
  Pull_Resistor pull_resistor_13 (.node(controlled_buffer_1_out[11]));
  Pull_Resistor pull_resistor_14 (.node(HLT));
  Pull_Resistor pull_resistor_15 (.node(RAM_LOAD));
  Pull_Resistor pull_resistor_16 (.node(SUB));
  not not_2 (not_2_out, controlled_buffer_4_out);
  Clock clock_1 (.out(clock_1_out));
  not not_3 (not_3_out, MO);
  LED led_1 (.in(PI));
  LED led_2 (.in(MO));
  LED led_3 (.in(OUT));
  LED led_4 (.in(PL));
  LED led_5 (.in(MIN));
  LED led_6 (.in(controlled_buffer_1_out[5]));
  LED led_7 (.in(IR));
  LED led_8 (.in(RAIN));
  LED led_9 (.in(RAOUT));
  LED led_10 (.in(RBIN));
  LED led_11 (.in(ALU));
  LED led_12 (.in(controlled_buffer_1_out[11]));
  LED led_13 (.in(HLT));
  LED led_14 (.in(RAM_LOAD));
  LED led_15 (.in(SUB));
  LED led_16 (.in(controlled_buffer_1_out[15]));
  or or_1 (or_6_out[3], B_out[5], B_out[6], B_out[7], B_out[0], B_out[1], B_out[2], B_out[4], B_out[3]);
  assign controlled_buffer_2_out = not_4_out ? clock_1_out : 1'bz;  // Controlled_Buffer controlled_buffer_2
  not not_4 (not_4_out, HLT);
  and and_1 (PO, not_3_out, MIN);
  Pull_Resistor #(.pull(1)) pull_resistor_17 (.node(pull_resistor_17_node));
  Button button_1 (.out(button_1_out));
  assign controlled_buffer_3_out = button_1_out ? pull_resistor_17_node : 1'bz;  // Controlled_Buffer controlled_buffer_3
  nor nor_1 (MCR, MO, OUT, PL, MIN, IR, RAIN, RAOUT, RBIN, ALU, HLT, RAM_LOAD, SUB);
  or or_2 (or_6_out[2], B_out[6], B_out[7], _3_out[7], _3_out[5], B_out[5], _3_out[6], _3_out[4], B_out[4]);
  assign controlled_buffer_4_out = PROG ? controlled_buffer_2_out : 1'bz;  // Controlled_Buffer controlled_buffer_4
  or or_3 (or_3_out, MIN, counter_2_q);
  not not_5 (not_5_out, PROG);
  assign controlled_buffer_3_out = button_3_out ? pull_resistor_18_node : 1'bz;  // Controlled_Buffer controlled_buffer_5
  Pull_Resistor #(.pull(1)) pull_resistor_18 (.node(pull_resistor_18_node));
  Register MAR (.D(controlled_buffer_6_out), .en(or_3_out), .Q(MAR_q), .clk(AD_L), .clr(controlled_buffer_3_out));
  assign controlled_buffer_6_out = not_5_out ? LD_DATA : 8'bz;  // Controlled_Buffer controlled_buffer_6
  assign controlled_buffer_7_out = PROG ? controlled_buffer_4_out : 1'bz;  // Controlled_Buffer controlled_buffer_7
  Pull_Resistor pull_resistor_19 (.node(controlled_buffer_3_out));
  Counter #(.width(1), .max('h1)) counter_2 (.Q(counter_2_q), .clk(button_3_out));  // open: load, D, count, carry, clr
  not not_6 (PROG, counter_2_q);
  or or_4 (or_6_out[1], B_out[0], B_out[1], _3_out[4], _3_out[5], _3_out[0], _3_out[1], B_out[4], B_out[5]);
  Register u_IR (
    .D(controlled_buffer_11_out), .en(IR), .Q({IR_q, pull_resistor_2_node[9:5]}),
    .clk(controlled_buffer_4_out), .clr(controlled_buffer_3_out));
  buf buffer_1 (buffer_1_out, controlled_buffer_4_out);
  assign RL = PROG ? buffer_1_out : 1'bz;  // Controlled_Buffer controlled_buffer_8
  Pull_Resistor #(.pull(1)) pull_resistor_20 (.node(pull_resistor_20_node));
  assign AD_L = PROG ? buffer_1_out : 1'bz;  // Controlled_Buffer controlled_buffer_9
  Counter PC (
    .load(PL), .D(controlled_buffer_11_out), .count(PI), .Q(PC_q), .clk(controlled_buffer_7_out),
    .clr(controlled_buffer_3_out));  // open: carry
  Button _0 (.out(_3_out[3]));
  Button _4 (.out(_3_out[7]));
  Button _8 (.out(B_out[3]));
  Button C (.out(B_out[7]));
  Button button_2 (.out(button_2_out));
  Button button_3 (.out(button_3_out));
  LED led_17 (.in(counter_2_q));
  // Probe on ram_1_data
  RAM ram_1 (.addr(MAR_q), .data(ram_1_data), .sel(pull_resistor_20_node), .clk(RL), .ld(not_7_out));  // open: clr
  not not_7 (not_7_out, or_5_out);
  or or_5 (or_5_out, RAM_LOAD, not_9_out);
  assign controlled_buffer_6_out = PROG ? controlled_buffer_11_out : 8'bz;  // Controlled_Buffer controlled_buffer_10
  assign controlled_buffer_11_out = PO ? PC_q : 8'bz;  // Controlled_Buffer controlled_buffer_11
  Button _1 (.out(_3_out[2]));
  Button _3 (.out(_3_out[0]));
  Button _2 (.out(_3_out[1]));
  Button _6 (.out(_3_out[5]));
  Button _7 (.out(_3_out[4]));
  Button _5 (.out(_3_out[6]));
  Button _9 (.out(B_out[2]));
  Button A (.out(B_out[1]));
  Button B (.out(B_out[0]));
  Button E (.out(B_out[5]));
  Button F (.out(B_out[4]));
  Button D (.out(B_out[6]));
  Button button_4 (.out(button_4_out));
  Hex_Digit_Display hex_digit_display_1 (.value(register_3_q[7:4]), .dp(demultiplexer_1_out0));
  Hex_Digit_Display hex_digit_display_2 (.value(register_3_q[3:0]), .dp(demultiplexer_1_out1));
  or or_6 (or_6_out[0], B_out[0], B_out[4], _3_out[4], _3_out[6], _3_out[0], _3_out[2], B_out[2], B_out[6]);
  not not_8 (not_8_out, PROG);
  assign ram_1_data = not_8_out ? LD_DATA : 8'bz;  // Controlled_Buffer controlled_buffer_12
  Pull_Resistor pull_resistor_21 (.node(pull_resistor_21_node));
  assign pull_resistor_21_node = PROG ? MO : 1'bz;  // Controlled_Buffer controlled_buffer_13
  assign controlled_buffer_11_out = pull_resistor_21_node ? ram_1_data : 8'bz;  // Controlled_Buffer controlled_buffer_14
  assign ram_1_data = RAM_LOAD ? controlled_buffer_11_out : 8'bz;  // Controlled_Buffer controlled_buffer_15
  not not_9 (not_9_out, PROG);
  DotMatrix #(.matrixcols(8), .matrixrows(1)) dotmatrix_1 (
    .col0(controlled_buffer_11_out[7]), .col1(controlled_buffer_11_out[6]),
    .col2(controlled_buffer_11_out[5]), .col3(controlled_buffer_11_out[4]),
    .col4(controlled_buffer_11_out[3]), .col5(controlled_buffer_11_out[2]),
    .col6(controlled_buffer_11_out[1]), .col7(controlled_buffer_11_out[0]));
  Hex_Digit_Display hex_digit_display_3 (.value(or_6_out));  // open: dp
  assign controlled_buffer_11_out = RAOUT ? RA_q : 8'bz;  // Controlled_Buffer controlled_buffer_16
  Pull_Resistor pull_resistor_22 (.node(controlled_buffer_11_out));
  Register RA (.D(controlled_buffer_11_out), .en(RAIN), .Q(RA_q), .clk(controlled_buffer_7_out));  // open: clr
  Register u_RB (.D(controlled_buffer_11_out), .en(RBIN), .Q(RB), .clk(controlled_buffer_7_out));  // open: clr
  assign controlled_buffer_11_out = ALU ? adder_1_out : 8'bz;  // Controlled_Buffer controlled_buffer_17
  Register RO (
    .D(controlled_buffer_11_out), .en(OUT), .Q(ROUT), .clk(controlled_buffer_7_out),
    .clr(controlled_buffer_3_out));
  assign RL = not_10_out ? button_4_out : 1'bz;  // Controlled_Buffer controlled_buffer_18
  assign AD_L = not_10_out ? button_2_out : 1'bz;  // Controlled_Buffer controlled_buffer_19
  Register #(.trigger("falling")) register_1 (.D(register_3_q), .Q(LD_DATA), .clk(or_7_out), .clr(PROG));  // open: en
  _8_bit_or u_8_bit_or_1 (.\input (_3_out), .Output(n8_bit_or_1_output));
  _8_bit_or u_8_bit_or_2 (.\input (B_out), .Output(n8_bit_or_2_output));
  inv inv_1 (.\output (inv_1_output), .\input (RB), .enable(SUB));
  DotMatrix #(.matrixcols(2), .matrixrows(1)) dotmatrix_2 (.col0(counter_3_q[1]), .col1(counter_3_q[0]));
  Counter #(.width(2), .max('h3)) counter_3 (.Q(counter_3_q), .clk(clock_2_out));  // open: load, D, count, carry, clr
  Clock clock_2 (.out(clock_2_out));
  not not_10 (not_10_out, PROG);
  or or_7 (or_7_out, n8_bit_or_1_output, n8_bit_or_2_output);
  Register #(.width(4)) register_2 (.D(or_6_out), .Q(register_3_q[7:4]), .clk(demultiplexer_1_out1));  // open: en, clr
  _8_bit_nor nor_2 (.\input (adder_1_out), .\output (pull_resistor_24_node[2]));
  \xor  \xor  (.in1(SUB), .in2(adder_1_cout), .out(pull_resistor_24_node[3]));
  Adder adder_1 (.a(RA_q), .b(inv_1_output), .out(adder_1_out), .cin(SUB), .cout(adder_1_cout));
  Hex_Digit_Display hex_digit_display_4 (.value(adder_1_out[7:4]));  // open: dp
  _7_Segment_Display u_7_segment_display_1 (
    .g(register_4_q[0]), .f(register_4_q[1]), .a(register_4_q[2]), .b(register_4_q[3]), .e(register_4_q[7]),
    .d(register_4_q[6]), .c(register_4_q[5]), .dp(register_4_q[4]));
  Pull_Resistor #(.pull(1)) pull_resistor_23 (.node(pull_resistor_23_node));
  Counter #(.width(1), .max('h1)) counter_4 (.Q(counter_4_q), .clk(or_7_out));  // open: load, D, count, carry, clr
  Demultiplexer #(.disabled(0), .enable("false")) demultiplexer_1 (
    .out0(demultiplexer_1_out0), .out1(demultiplexer_1_out1), .in(pull_resistor_23_node), .sel(counter_4_q));
  Register #(.width(4)) register_3 (.D(or_6_out), .Q(register_3_q[3:0]), .clk(demultiplexer_1_out0));  // open: en, clr
  DotMatrix #(.matrixcols(4), .matrixrows(1)) dotmatrix_3 (
    .col0(pull_resistor_24_node[3]), .col1(pull_resistor_24_node[2]), .col2(pull_resistor_24_node[1]),
    .col3(pull_resistor_24_node[1]));
  Pull_Resistor pull_resistor_24 (.node(pull_resistor_24_node[1]));
  Hex_Digit_Display hex_digit_display_5 (.value(adder_1_out[3:0]));  // open: dp
  DotMatrix #(.matrixcols(10), .matrixrows(1)) dotmatrix_4 (
    .col0(counter_3_q[1]), .col1(counter_3_q[0]), .col2(ROUT[7]), .col3(ROUT[6]), .col4(ROUT[5]),
    .col5(ROUT[4]), .col6(ROUT[3]), .col7(ROUT[2]), .col8(ROUT[1]), .col9(ROUT[0]));
  _8_bit_or u_8_bit_or_3 (.\input (demultiplexer_2_out2), .Output(n8_bit_or_3_output));
  Register register_4 (
    .D(demultiplexer_2_out2), .en(n8_bit_or_3_output), .Q(register_4_q), .clk(clock_2_out));  // open: clr
  _7_Segment_Display u_7_segment_display_2 (
    .g(register_6_q[0]), .f(register_6_q[1]), .a(register_6_q[2]), .b(register_6_q[3]), .e(register_6_q[7]),
    .d(register_6_q[6]), .c(register_6_q[5]), .dp(register_6_q[4]));
  DotMatrix #(.matrixcols(4), .matrixrows(1)) dotmatrix_5 (
    .col0(register_5_q[3]), .col1(register_5_q[2]), .col2(register_5_q[1]), .col3(register_5_q[0]));
  Register #(.width(4)) register_5 (
    .D({pull_resistor_24_node, pull_resistor_24_node[1]}), .en(ALU), .Q(register_5_q),
    .clk(controlled_buffer_7_out));  // open: clr
  ROM #(.addrWidth(10)) rom_2 (.addr({counter_3_q, ROUT}), .data(rom_2_data));  // open: sel
  Demultiplexer #(.select(2), .width(8), .disabled(0), .enable("false")) demultiplexer_2 (
    .out0(demultiplexer_2_out0), .out1(demultiplexer_2_out1), .out2(demultiplexer_2_out2), .in(rom_2_data),
    .sel(counter_3_q));  // open: out3
  _8_bit_or u_8_bit_or_4 (.\input (demultiplexer_2_out1), .Output(n8_bit_or_4_output));
  Register register_6 (
    .D(demultiplexer_2_out1), .en(n8_bit_or_4_output), .Q(register_6_q), .clk(clock_2_out));  // open: clr
  _7_Segment_Display u_7_segment_display_3 (
    .g(register_7_q[0]), .f(register_7_q[1]), .a(register_7_q[2]), .b(register_7_q[3]), .e(register_7_q[7]),
    .d(register_7_q[6]), .c(register_7_q[5]), .dp(register_7_q[4]));
  _8_bit_or u_8_bit_or_5 (.\input (demultiplexer_2_out0), .Output(n8_bit_or_5_output));
  Register register_7 (
    .D(demultiplexer_2_out0), .en(n8_bit_or_5_output), .Q(register_7_q), .clk(clock_2_out));  // open: clr

  // Notes on the sheet:
  //   contents of rom_1 (hex, n*v repeats v):
  //   4*31 4*42 24*800 4*31 4*42 4*30 4*a 16*800 4*31 4*42 4*30 4*12 4*a 12*800 4*31 4*42 31 31 30 30 800
  //   800 a a 16*800 4*31 4*42 4*30 4*82 4*801 12*800 4*31 4*42 4*30 4*12 4*82 4*801 8*800 4*31 4*42 4*104
  //   20*800 4*31 4*42 4*30 4*202 4*801 12*800 4*31 4*42 4*30 4*6 4*801 12*800 4*31 4*42 4*30 4*12 4*6
  //   4*801 8*800 4*31 4*42 4*30 4*203 4*8480 12*800 4*31 4*42 4*30 4*12 4*202 4*8480 4*801 4*800 4*31
  //   4*42 4*30 4*4203 4*c480 12*800 4*31 4*42 4*30 4*12 4*4202 4*c480 4*801 4*800 4*31 4*42 4*30 4*12
  //   4*2100 4*801 8*800 4*31 4*42 31 30 31 30 800 a 800 a 16*800 4*31 4*42 4*31 20*800 4*31 4*42 4*31
  //   20*800 4*31 4*42 4*800 20*0 4*31 4*42 4*800 20*0 4*31 4*42 4*800 20*0 4*31 4*42 4*800 20*0 4*31 4*42
  //   4*800 20*0 4*31 4*42 4*800 20*0 4*31 4*42 4*800 20*0 4*31 4*42 4*800 20*0 4*31 4*42 4*800 20*0 4*31
  //   4*42 4*800 20*0 4*31 4*42 4*800 20*0 4*31 4*42 4*800 20*0 4*31 4*42 4*800 20*0 4*31 4*42 4*1000
  //   20*800 4*31 4*42 4*800 20*0 4*31 4*42 4*800 20*0 4*31 4*42 4*800 20*0 4*31 4*42 4*800 20*0 4*31 4*42
  //   4*800 20*0 4*31 4*42 4*800 20*0 4*31 4*42 4*800 20*0 4*31 4*42 4*800 20*0 4*31 4*42 4*800 20*0 4*31
  //   4*42 4*800 20*0 4*31 4*42 4*800 20*0 4*31 4*42 4*800 20*0 4*31 4*42 4*800 20*0 4*31 4*42 4*800 20*0
  //   4*31 4*42 4*800 20*0 4*31 4*42 4*800 20*0 4*31 4*42 4*800 20*0 4*31 4*42 4*800 20*0 4*31 4*42 4*800
  //   20*0 4*31 4*42 4*800 20*0 4*31 4*42 4*800 20*0 4*31 4*42 4*800 20*0 4*31 4*42 4*800 20*0 4*31 4*42
  //   4*800 20*0 4*31 4*42 4*800 20*0 4*31 4*42 4*800 20*0 4*31 4*42 4*800 20*0 4*31 4*42 4*800 20*0 4*31
  //   4*42 4*800 20*0 4*31 4*42 4*800 0 ffff 18*0 4*31 4*42 4*800 20*0 4*31 4*42 4*800
  //   RESET
  //   Program
  //   Address
  //   Data
  //   contents of rom_2 (hex, n*v repeats v):
  //   ee 28 cd 6d 2b 67 e7 2c ef 6f ee 28 cd 6d 2b 67 e7 2c ef 6f ee 28 cd 6d 2b 67 e7 2c ef 6f ee 28 cd
  //   6d 2b 67 e7 2c ef 6f ee 28 cd 6d 2b 67 e7 2c ef 6f ee 28 cd 6d 2b 67 e7 2c ef 6f ee 28 cd 6d 2b 67
  //   e7 2c ef 6f ee 28 cd 6d 2b 67 e7 2c ef 6f ee 28 cd 6d 2b 67 e7 2c ef 6f ee 28 cd 6d 2b 67 e7 2c ef
  //   6f ee 28 cd 6d 2b 67 e7 2c ef 6f ee 28 cd 6d 2b 67 e7 2c ef 6f ee 28 cd 6d 2b 67 e7 2c ef 6f ee 28
  //   cd 6d 2b 67 e7 2c ef 6f ee 28 cd 6d 2b 67 e7 2c ef 6f ee 28 cd 6d 2b 67 e7 2c ef 6f ee 28 cd 6d 2b
  //   67 e7 2c ef 6f ee 28 cd 6d 2b 67 e7 2c ef 6f ee 28 cd 6d 2b 67 e7 2c ef 6f ee 28 cd 6d 2b 67 e7 2c
  //   ef 6f ee 28 cd 6d 2b 67 e7 2c ef 6f ee 28 cd 6d 2b 67 e7 2c ef 6f ee 28 cd 6d 2b 67 e7 2c ef 6f ee
  //   28 cd 6d 2b 67 e7 2c ef 6f ee 28 cd 6d 2b 67 e7 2c ef 6f ee 28 cd 6d 2b 67 10*ee 10*28 10*cd 10*6d
  //   10*2b 10*67 10*e7 10*2c 10*ef 10*6f 10*ee 10*28 10*cd 10*6d 10*2b 10*67 10*e7 10*2c 10*ef 10*6f
  //   10*ee 10*28 10*cd 10*6d 10*2b 6*67 100*ee 100*28 56*cd
endmodule

module inv (
  input  enable,
  input  [7:0] \input ,
  output [7:0] \output 
);

  xor xor_1 (\output [7], \input [7], enable);
  xor xor_2 (\output [6], \input [6], enable);
  xor xor_3 (\output [5], \input [5], enable);
  xor xor_4 (\output [4], \input [4], enable);
  xor xor_5 (\output [3], \input [3], enable);
  xor xor_6 (\output [2], \input [2], enable);
  xor xor_7 (\output [1], \input [1], enable);
  xor xor_8 (\output [0], \input [0], enable);

  // Notes on the sheet:
  //   input: pull=down
endmodule

module _8_bit_nor (
  input  [7:0] \input ,
  output \output 
);

  nor nor_1 (\output , \input [0], \input [1], \input [2], \input [3], \input [4], \input [5], \input [6], \input [7]);

  // Notes on the sheet:
  //   output: pull=down
  //   input: pull=down
endmodule

module \nand  (
  input  in_1,
  input  in_2,
  output out_3
);

  nand nand_1 (out_3, in_1, in_2);

  // Notes on the sheet:
  //   out_3: pull=down
  //   in_2: pull=down
endmodule

module \xor  (
  input  in1,
  input  in2,
  output out
);

  xor xor_1 (out, in1, in2);

  // Notes on the sheet:
  //   in2: pull=down
  //   in1: pull=down
endmodule

module _8_bit_or (
  input  [7:0] \input ,
  output Output
);

  or or_1 (Output, \input [0], \input [1], \input [2], \input [3], \input [4], \input [5], \input [6], \input [7]);

  // Notes on the sheet:
  //   input: pull=down
  //   Output: pull=down
endmodule
