// Logisim project computer-ramload.circ as structural Verilog: 5 circuits, main circuit main
module main (
);

  wire adder_1_cout, buffer_1_out, buffer_2_out, buffer_3_out, button_1_out, button_2_out, clock_1_out,
       clock_2_out, clock_3_out, controlled_buffer_1_out, controlled_buffer_2_out, controlled_buffer_4_out,
       controlled_buffer_6_out, controlled_buffer_10_out, controlled_buffer_15_out, not_1_out, not_2_out,
       not_3_out, not_4_out, not_5_out, or_1_out, or_2_out, or_3_out, pull_resistor_3_node,
       pull_resistor_4_node, pull_resistor_8_node;
  wire [1:0] counter_2_q, counter_3_q, counter_3_q_2, counter_3_q_3, counter_3_q_4, register_4_q;
  wire [2:0] pull_resistor_1_node;
  wire [3:0] register_2_q;
  wire [3:1] pull_resistor_10_node;
  wire [4:2] counter_1_q;
  wire [7:0] adder_1_out, controlled_buffer_3_out, controlled_buffer_7_out, controlled_buffer_13_out,
       demultiplexer_1_out0, demultiplexer_1_out1, demultiplexer_1_out2, inv_1_output, IR_q, MAR_q, PC_q,
       RA_q, ram_1_data, RB_q, register_1_q, register_3_q, register_5_q, RO_q, rom_2_data, rom_3_data;
  wire [15:0] rom_1_data;

  not not_1 (not_1_out, rom_1_data[11]);
  DotMatrix #(.inputtype("row"), .matrixcols(1), .matrixrows(16), .dotshape("circle")) dotmatrix_1 (
    .row0(rom_1_data[0]), .row1(rom_1_data[1]), .row2(rom_1_data[2]), .row3(rom_1_data[3]),
    .row4(rom_1_data[4]), .row5(rom_1_data[5]), .row6(rom_1_data[6]), .row7(rom_1_data[7]),
    .row8(rom_1_data[8]), .row9(rom_1_data[9]), .row10(rom_1_data[10]), .row11(rom_1_data[11]),
    .row12(rom_1_data[12]), .row13(rom_1_data[13]), .row14(rom_1_data[14]), .row15(rom_1_data[15]));
  Pull_Resistor pull_resistor_1 (.node(pull_resistor_1_node));
  DotMatrix #(.inputtype("row"), .matrixcols(1), .matrixrows(11)) dotmatrix_2 (
    .row0(register_2_q[2]), .row1(register_2_q[3]), .row2(counter_1_q[2]), .row3(counter_1_q[3]),
    .row4(counter_1_q[4]), .row5(IR_q[0]), .row6(IR_q[1]), .row7(IR_q[2]), .row8(IR_q[3]), .row9(IR_q[4]),
    .row10(IR_q[5]));
  not not_2 (not_2_out, controlled_buffer_2_out);
  Counter #(.width(3), .max('h7)) counter_1 (
    .load(rom_1_data[11]), .D(pull_resistor_1_node), .count(not_1_out), .Q(counter_1_q), .clk(not_2_out),
    .clr(button_1_out));  // open: carry
  ROM #(.addrWidth(11), .dataWidth(16)) rom_1 (
    .addr({IR_q[5:0], counter_1_q, register_2_q[3:2]}), .data(rom_1_data));  // open: sel
  not not_3 (not_3_out, rom_1_data[12]);
  Clock clock_1 (.out(clock_1_out));
  assign controlled_buffer_1_out = not_3_out ? clock_1_out : 1'bz;  // Controlled_Buffer controlled_buffer_1
  assign controlled_buffer_2_out = buffer_1_out ? controlled_buffer_1_out : 1'bz;  // Controlled_Buffer controlled_buffer_2
  Register IR (
    .D(controlled_buffer_7_out), .en(rom_1_data[6]), .Q(IR_q), .clk(controlled_buffer_2_out),
    .clr(button_1_out));
  Pull_Resistor pull_resistor_2 (.node(controlled_buffer_2_out));
  assign controlled_buffer_3_out = buffer_1_out ? MAR_q : 8'bz;  // Controlled_Buffer controlled_buffer_3
  Register MAR (
    .D(controlled_buffer_7_out), .en(rom_1_data[4]), .Q(MAR_q), .clk(controlled_buffer_2_out),
    .clr(button_1_out));
  Counter PC (
    .load(rom_1_data[3]), .D(controlled_buffer_7_out), .count(rom_1_data[0]), .Q(PC_q),
    .clk(controlled_buffer_2_out), .clr(button_1_out));  // open: carry
  DotMatrix #(.matrixcols(8), .matrixrows(1)) dotmatrix_3 (
    .col0(IR_q[7]), .col1(IR_q[6]), .col2(IR_q[5]), .col3(IR_q[4]), .col4(IR_q[3]), .col5(IR_q[2]),
    .col6(IR_q[1]), .col7(IR_q[0]));
  buf buffer_1 (buffer_1_out, buffer_2_out);
  Pull_Resistor #(.pull(1)) pull_resistor_3 (.node(pull_resistor_3_node));
  assign controlled_buffer_4_out = buffer_3_out ? rom_1_data[13] : 1'bz;  // Controlled_Buffer controlled_buffer_4
  assign controlled_buffer_2_out = pull_resistor_4_node ? controlled_buffer_15_out : 1'bz;  // Controlled_Buffer controlled_buffer_5
  Pull_Resistor pull_resistor_4 (.node(pull_resistor_4_node));
  RAM ram_1 (
    .addr(controlled_buffer_3_out), .data(ram_1_data), .sel(pull_resistor_3_node),
    .clk(controlled_buffer_2_out), .ld(not_4_out));  // open: clr
  not not_4 (not_4_out, controlled_buffer_6_out);
  assign controlled_buffer_6_out = buffer_3_out ? controlled_buffer_4_out : 1'bz;  // Controlled_Buffer controlled_buffer_6
  assign controlled_buffer_7_out = rom_1_data[5] ? PC_q : 8'bz;  // Controlled_Buffer controlled_buffer_7
  assign controlled_buffer_3_out = pull_resistor_4_node ? {counter_3_q_4, counter_3_q_3, counter_3_q_2, counter_3_q} : 8'bz;  // Controlled_Buffer controlled_buffer_8
  assign controlled_buffer_6_out = pull_resistor_4_node ? pull_resistor_4_node : 1'bz;  // Controlled_Buffer controlled_buffer_9
  not not_5 (not_5_out, pull_resistor_4_node);
  Pull_Resistor pull_resistor_5 (.node(controlled_buffer_6_out));
  buf buffer_2 (buffer_2_out, not_5_out);
  DotMatrix #(.inputtype("row"), .matrixcols(1), .matrixrows(8)) dotmatrix_4 (
    .row0(ram_1_data[0]), .row1(ram_1_data[1]), .row2(ram_1_data[2]), .row3(ram_1_data[3]),
    .row4(ram_1_data[4]), .row5(ram_1_data[5]), .row6(ram_1_data[6]), .row7(ram_1_data[7]));
  buf buffer_3 (buffer_3_out, buffer_2_out);
  assign controlled_buffer_10_out = buffer_3_out ? controlled_buffer_4_out : 1'bz;  // Controlled_Buffer controlled_buffer_10
  Pull_Resistor pull_resistor_6 (.node(controlled_buffer_10_out));
  assign controlled_buffer_7_out = rom_1_data[1] ? ram_1_data : 8'bz;  // Controlled_Buffer controlled_buffer_11
  assign ram_1_data = controlled_buffer_10_out ? controlled_buffer_7_out : 8'bz;  // Controlled_Buffer controlled_buffer_12
  Pull_Resistor pull_resistor_7 (.node(controlled_buffer_4_out));
  DotMatrix #(.matrixcols(8), .matrixrows(1), .dotshape("circle")) dotmatrix_5 (
    .col0(controlled_buffer_7_out[7]), .col1(controlled_buffer_7_out[6]), .col2(controlled_buffer_7_out[5]),
    .col3(controlled_buffer_7_out[4]), .col4(controlled_buffer_7_out[3]), .col5(controlled_buffer_7_out[2]),
    .col6(controlled_buffer_7_out[1]), .col7(controlled_buffer_7_out[0]));
  assign controlled_buffer_13_out = pull_resistor_4_node ? rom_3_data : 8'bz;  // Controlled_Buffer controlled_buffer_13
  assign ram_1_data = controlled_buffer_13_out;  // Buffer buffer_4, 8 bits wide
  assign controlled_buffer_7_out = rom_1_data[8] ? RA_q : 8'bz;  // Controlled_Buffer controlled_buffer_14
  _7_Segment_Display u_7_segment_display_1 (
    .g(rom_2_data[0]), .f(rom_2_data[1]), .a(rom_2_data[2]), .b(rom_2_data[3]), .e(rom_2_data[7]),
    .d(rom_2_data[6]), .c(rom_2_data[5]), .dp(rom_2_data[4]));
  Clock clock_2 (.out(clock_2_out));
  assign controlled_buffer_15_out = pull_resistor_4_node ? clock_2_out : 1'bz;  // Controlled_Buffer controlled_buffer_15
  Register RA (.D(controlled_buffer_7_out), .en(rom_1_data[7]), .Q(RA_q), .clk(controlled_buffer_2_out));  // open: clr
  inv inv_1 (.\output (inv_1_output), .\input (RB_q), .enable(rom_1_data[14]));
  Register RB (.D(controlled_buffer_7_out), .en(rom_1_data[9]), .Q(RB_q), .clk(controlled_buffer_2_out));  // open: clr
  assign controlled_buffer_7_out = rom_1_data[10] ? adder_1_out : 8'bz;  // Controlled_Buffer controlled_buffer_16
  Register RO (
    .D(controlled_buffer_7_out), .en(rom_1_data[2]), .Q(RO_q), .clk(controlled_buffer_2_out),
    .clr(button_1_out));
  Button button_1 (.out(button_1_out));
  Counter #(.width(2), .max('h3)) counter_2 (.Q(counter_2_q), .clk(clock_3_out));  // open: load, D, count, carry, clr
  Clock clock_3 (.out(clock_3_out));
  Pull_Resistor #(.pull(1)) pull_resistor_8 (.node(pull_resistor_8_node));
  Pull_Resistor pull_resistor_9 (.node(controlled_buffer_15_out));
  _8_bit_nor \nor  (.\input (adder_1_out), .\output (pull_resistor_10_node[2]));
  Adder adder_1 (.a(RA_q), .b(inv_1_output), .out(adder_1_out), .cin(rom_1_data[14]), .cout(adder_1_cout));
  DotMatrix #(.matrixcols(2), .matrixrows(1)) dotmatrix_6 (.col0(counter_2_q[1]), .col1(counter_2_q[0]));
  _7_Segment_Display u_7_segment_display_2 (
    .g(register_1_q[0]), .f(register_1_q[1]), .a(register_1_q[2]), .b(register_1_q[3]), .e(register_1_q[7]),
    .d(register_1_q[6]), .c(register_1_q[5]), .dp(register_1_q[4]));
  Counter #(.ongoal("stay")) counter_3 (
    .count(pull_resistor_8_node), .Q({counter_3_q_4, counter_3_q_3, counter_3_q_2, counter_3_q}),
    .clk(controlled_buffer_15_out), .clr(button_2_out));  // open: load, D, carry
  Button button_2 (.out(button_2_out));
  DotMatrix #(.matrixcols(4), .matrixrows(1)) dotmatrix_7 (
    .col0(pull_resistor_10_node[3]), .col1(pull_resistor_10_node[2]), .col2(pull_resistor_10_node[1]),
    .col3(pull_resistor_10_node[1]));
  \xor  \xor  (.in1(rom_1_data[14]), .in2(adder_1_cout), .out(pull_resistor_10_node[3]));
  Pull_Resistor pull_resistor_10 (.node(pull_resistor_10_node[1]));
  Hex_Digit_Display hex_digit_display_1 (.value(adder_1_out[3:0]));  // open: dp
  Hex_Digit_Display hex_digit_display_2 (.value(adder_1_out[7:4]));  // open: dp
  DotMatrix #(.matrixcols(10), .matrixrows(1)) dotmatrix_8 (
    .col0(counter_2_q[1]), .col1(counter_2_q[0]), .col2(RO_q[7]), .col3(RO_q[6]), .col4(RO_q[5]),
    .col5(RO_q[4]), .col6(RO_q[3]), .col7(RO_q[2]), .col8(RO_q[1]), .col9(RO_q[0]));
  Register register_1 (.D(demultiplexer_1_out2), .en(or_2_out), .Q(register_1_q), .clk(clock_3_out));  // open: clr
  _7_Segment_Display u_7_segment_display_3 (
    .g(register_3_q[0]), .f(register_3_q[1]), .a(register_3_q[2]), .b(register_3_q[3]), .e(register_3_q[7]),
    .d(register_3_q[6]), .c(register_3_q[5]), .dp(register_3_q[4]));
  DotMatrix #(.matrixcols(4), .matrixrows(1)) dotmatrix_9 (
    .col0(register_2_q[3]), .col1(register_2_q[2]), .col2(register_2_q[1]), .col3(register_2_q[0]));
  Register #(.width(4)) register_2 (
    .D({pull_resistor_10_node, pull_resistor_10_node[1]}), .en(rom_1_data[15]), .Q(register_2_q),
    .clk(controlled_buffer_2_out));  // open: clr
  ROM #(.addrWidth(10)) rom_2 (.addr({counter_2_q, RO_q}), .data(rom_2_data));  // open: sel
  Register register_3 (.D(demultiplexer_1_out1), .en(or_3_out), .Q(register_3_q), .clk(clock_3_out));  // open: clr
  _7_Segment_Display u_7_segment_display_4 (
    .g(register_5_q[0]), .f(register_5_q[1]), .a(register_5_q[2]), .b(register_5_q[3]), .e(register_5_q[7]),
    .d(register_5_q[6]), .c(register_5_q[5]), .dp(register_5_q[4]));
  Register #(.width(2)) register_4 (.Q(register_4_q));  // open: D, en, clk, clr
  Demultiplexer #(.select(2), .width(8), .disabled(0), .enable("false")) demultiplexer_1 (
    .out0(demultiplexer_1_out0), .out1(demultiplexer_1_out1), .out2(demultiplexer_1_out2), .in(rom_2_data),
    .sel(counter_2_q));  // open: out3
  or or_1 (or_1_out, demultiplexer_1_out0[0], demultiplexer_1_out0[1], demultiplexer_1_out0[2], demultiplexer_1_out0[3], demultiplexer_1_out0[4], demultiplexer_1_out0[5], demultiplexer_1_out0[6], demultiplexer_1_out0[7]);
  Register register_5 (.D(demultiplexer_1_out0), .en(or_1_out), .Q(register_5_q), .clk(clock_3_out));  // open: clr
  or or_2 (or_2_out, demultiplexer_1_out2[0], demultiplexer_1_out2[1], demultiplexer_1_out2[2], demultiplexer_1_out2[3], demultiplexer_1_out2[4], demultiplexer_1_out2[5], demultiplexer_1_out2[6], demultiplexer_1_out2[7]);
  or or_3 (or_3_out, demultiplexer_1_out1[0], demultiplexer_1_out1[1], demultiplexer_1_out1[2], demultiplexer_1_out1[3], demultiplexer_1_out1[4], demultiplexer_1_out1[5], demultiplexer_1_out1[6], demultiplexer_1_out1[7]);
  ROM #(.addrWidth(10)) rom_3 (
    .addr({register_4_q, counter_3_q_4, counter_3_q_3, counter_3_q_2, counter_3_q}), .data(rom_3_data));  // open: sel

  // Notes on the sheet:
  //   contents of rom_1 (hex, n*v repeats v):
  //   4*31 4*42 24*800 4*31 4*42 4*30 4*a 16*800 4*31 4*42 4*30 4*12 4*a 12*800 4*31 4*42 31 31 30 30 800
  //   800 a a 16*800 4*31 4*42 4*30 4*82 4*801 12*800 4*31 4*42 4*30 4*12 4*82 4*801 8*800 4*31 4*42 4*104
  //   20*800 4*31 4*42 4*30 4*202 4*801 12*800 4*31 4*42 4*30 4*6 4*801 12*800 4*31 4*42 4*30 4*12 4*6
  //   4*801 8*800 4*31 4*42 4*30 4*203 4*8480 12*800 4*31 4*42 4*30 4*12 4*202 4*8480 4*801 4*800 4*31
  //   4*42 4*30 4*4203 4*c480 12*800 4*31 4*42 4*30 4*12 4*4202 4*c480 4*801 4*800 4*31 4*42 4*30 4*12
  //   4*2100 4*801 8*800 4*31 4*42 31 30 31 30 800 a 800 a 16*800 4*31 4*42 4*31 20*800 4*31 4*42 4*31
  //   20*800 4*31 4*42 4*800 20*0 4*31 4*42 4*800 20*0 4*31 4*42 4*800 20*0 4*31 4*42 4*800 20*0 4*31 4*42
  //   4*800 20*0 4*31 4*42 4*800 20*0 4*31 4*42 4*800 20*0 4*31 4*42 4*800 20*0 4*31 4*42 4*800 20*0 4*31
  //   4*42 4*800 20*0 4*31 4*42 4*800 20*0 4*31 4*42 4*800 20*0 4*31 4*42 4*800 20*0 4*31 4*42 4*1000
  //   20*800 4*31 4*42 4*800 20*0 4*31 4*42 4*800 20*0 4*31 4*42 4*800 20*0 4*31 4*42 4*800 20*0 4*31 4*42
  //   4*800 20*0 4*31 4*42 4*800 20*0 4*31 4*42 4*800 20*0 4*31 4*42 4*800 20*0 4*31 4*42 4*800 20*0 4*31
  //   4*42 4*800 20*0 4*31 4*42 4*800 20*0 4*31 4*42 4*800 20*0 4*31 4*42 4*800 20*0 4*31 4*42 4*800 20*0
  //   4*31 4*42 4*800 20*0 4*31 4*42 4*800 20*0 4*31 4*42 4*800 20*0 4*31 4*42 4*800 20*0 4*31 4*42 4*800
  //   20*0 4*31 4*42 4*800 20*0 4*31 4*42 4*800 20*0 4*31 4*42 4*800 20*0 4*31 4*42 4*800 20*0 4*31 4*42
  //   4*800 20*0 4*31 4*42 4*800 20*0 4*31 4*42 4*800 20*0 4*31 4*42 4*800 20*0 4*31 4*42 4*800 20*0 4*31
  //   4*42 4*800 20*0 4*31 4*42 4*800 20*0 4*31 4*42 4*800 20*0 4*31 4*42 4*800
  //   contents of rom_2 (hex, n*v repeats v):
  //   ee 28 cd 6d 2b 67 e7 2c ef 6f ee 28 cd 6d 2b 67 e7 2c ef 6f ee 28 cd 6d 2b 67 e7 2c ef 6f ee 28 cd
  //   6d 2b 67 e7 2c ef 6f ee 28 cd 6d 2b 67 e7 2c ef 6f ee 28 cd 6d 2b 67 e7 2c ef 6f ee 28 cd 6d 2b 67
  //   e7 2c ef 6f ee 28 cd 6d 2b 67 e7 2c ef 6f ee 28 cd 6d 2b 67 e7 2c ef 6f ee 28 cd 6d 2b 67 e7 2c ef
  //   6f ee 28 cd 6d 2b 67 e7 2c ef 6f ee 28 cd 6d 2b 67 e7 2c ef 6f ee 28 cd 6d 2b 67 e7 2c ef 6f ee 28
  //   cd 6d 2b 67 e7 2c ef 6f ee 28 cd 6d 2b 67 e7 2c ef 6f ee 28 cd 6d 2b 67 e7 2c ef 6f ee 28 cd 6d 2b
  //   67 e7 2c ef 6f ee 28 cd 6d 2b 67 e7 2c ef 6f ee 28 cd 6d 2b 67 e7 2c ef 6f ee 28 cd 6d 2b 67 e7 2c
  //   ef 6f ee 28 cd 6d 2b 67 e7 2c ef 6f ee 28 cd 6d 2b 67 e7 2c ef 6f ee 28 cd 6d 2b 67 e7 2c ef 6f ee
  //   28 cd 6d 2b 67 e7 2c ef 6f ee 28 cd 6d 2b 67 e7 2c ef 6f ee 28 cd 6d 2b 67 10*ee 10*28 10*cd 10*6d
  //   10*2b 10*67 10*e7 10*2c 10*ef 10*6f 10*ee 10*28 10*cd 10*6d 10*2b 10*67 10*e7 10*2c 10*ef 10*6f
  //   10*ee 10*28 10*cd 10*6d 10*2b 6*67 100*ee 100*28 56*cd
  //   contents of rom_3 (hex, n*v repeats v):
  //   5 ff e fd 6 5 fe c 1 e fa 5 ff c 1 e fc 5 fc e fb 5 fd b ff e fd 5 fb c 1 e fb 5 fd f 27 1 15 6 e ff
  //   5 fa c 1 e fa f 34 1 11 1f 201*0 5 3 5 fd d fe f 13 3 19 e fd 5 ff a 1 e ff 6 1 0 5 ff a 1 6 1f 5 ff
  //   6 1f 224*0 70 1b 0 5 fe b ff 3 12 6 e ff b fe 3 12 6 e fe 1 2 1f 235*0 1 0 4 a 6 c 1 6 f a 1 3 1f
endmodule

module inv (
  input  enable,
  input  [7:0] \input ,
  output [7:0] \output 
);

  xor xor_1 (\output [7], \input [7], enable);
  xor xor_2 (\output [6], \input [6], enable);
  xor xor_3 (\output [5], \input [5], enable);
  xor xor_4 (\output [4], \input [4], enable);
  xor xor_5 (\output [3], \input [3], enable);
  xor xor_6 (\output [1], \input [1], enable);
  xor xor_7 (\output [2], \input [2], enable);
  xor xor_8 (\output [0], \input [0], enable);

  // Notes on the sheet:
  //   input: pull=down
endmodule

module _8_bit_nor (
  input  [7:0] \input ,
  output \output 
);

  nor nor_1 (\output , \input [0], \input [1], \input [2], \input [3], \input [4], \input [5], \input [6], \input [7]);

  // Notes on the sheet:
  //   input: pull=down
  //   output: pull=down
endmodule

module \nand  (
  input  in_1,
  input  in_2,
  output out_3
);

  nand nand_1 (out_3, in_1, in_2);

  // Notes on the sheet:
  //   out_3: pull=down
  //   in_2: pull=down
endmodule

module \xor  (
  input  in1,
  input  in2,
  output out
);

  xor xor_1 (out, in1, in2);

  // Notes on the sheet:
  //   in1: pull=down
  //   in2: pull=down
endmodule
