// Logisim project computer2.circ as structural Verilog: 6 circuits, main circuit main
module main (
);

  wire adder_1_cout, adder_2_cout, ALU_OUT, and_2_out, and_3_out, AOUT, button_1_out, button_2_out,
       button_3_out, button_4_out, CLK, clock_2_out, controlled_buffer_11_out, counter_1_q, DMA_REQ,
       FLAGS_RESET, HLT, IR_IN, LEDS_OUT, MAR_IN, n16_nor_1_output, not_1_out, not_2_out, not_3_out,
       not_4_out, not_5_out, not_6_out, not_7_out, or_1_out, OUTPUT, PC_IN, PC_INC, PC_OUT, PCLK,
       programmer_1_programming_enabled, pull_resistor_2_node, pull_resistor_3_node, RA_IN, RA_OUT, RAM_IN,
       RAM_OUT, RB_IN, s_r_ff_1_q, SUB, t_ff_1_q, t_ff_1_qn, t_ff_2_q, t_ff_2_qn, t_ff_3_q, t_ff_3_qn,
       UC_RESET;
  wire [1:0] FLAGS_OUT, n16_nor_2_output;
  wire [2:0] UC;
  wire [3:0] adder_1_out_2, display_1_out_2, display_1_out_2_2, display_1_out_3, display_1_out_3_2,
       register_1_q, register_2_q;
  wire [4:0] INST;
  wire [7:0] adder_1_out, BUS, controlled_buffer_6_out, counter_2_q, demultiplexer_1_out0,
       demultiplexer_1_out1, display_1_out_4, inverter_1_output, MAR_q, OUTPUT_DATA, PC_q, RA, RB,
       register_3_q, register_4_q, SUM;
  wire [11:11] pull_resistor_1_node;
  wire [15:0] demultiplexer_2_out0, demultiplexer_2_out1, demultiplexer_2_out2, demultiplexer_2_out3,
       demultiplexer_2_out4, demultiplexer_2_out5, demultiplexer_2_out6, demultiplexer_2_out7,
       demultiplexer_2_out8, demultiplexer_2_out9, demultiplexer_2_out10, demultiplexer_2_out11,
       demultiplexer_2_out12, demultiplexer_2_out13, demultiplexer_2_out14, demultiplexer_2_out15, rom_1_data;

  Clock clock_1 (.out(PCLK));
  Pull_Resistor pull_resistor_1 (.node({AOUT, SUB, RAM_IN, HLT, pull_resistor_1_node[11], ALU_OUT, RB_IN, RA_OUT, RA_IN, IR_IN, LEDS_OUT, MAR_IN, PC_IN, OUTPUT, RAM_OUT, PC_INC}));
  assign CLK = not_1_out ? PCLK : 1'bz;  // Controlled_Buffer controlled_buffer_1
  not not_1 (not_1_out, HLT);
  not not_2 (not_2_out, DMA_REQ);
  assign {AOUT, SUB, RAM_IN, HLT, pull_resistor_1_node[11], ALU_OUT, RB_IN, RA_OUT, RA_IN, IR_IN, LEDS_OUT, MAR_IN, PC_IN, OUTPUT, RAM_OUT, PC_INC} = not_2_out ? rom_1_data : 16'bz;  // Controlled_Buffer controlled_buffer_2
  LED led_1 (.in(PC_INC));
  LED led_2 (.in(RAM_OUT));
  LED led_3 (.in(OUTPUT));
  LED led_4 (.in(PC_IN));
  LED led_5 (.in(MAR_IN));
  LED led_6 (.in(LEDS_OUT));
  LED led_7 (.in(IR_IN));
  LED led_8 (.in(RA_IN));
  LED led_9 (.in(RA_OUT));
  LED led_10 (.in(RB_IN));
  LED led_11 (.in(ALU_OUT));
  LED led_12 (.in(pull_resistor_1_node[11]));
  LED led_13 (.in(HLT));
  LED led_14 (.in(RAM_IN));
  LED led_15 (.in(SUB));
  LED led_16 (.in(AOUT));
  not not_3 (not_3_out, RAM_OUT);
  not not_4 (not_4_out, DMA_REQ);
  and and_1 (PC_OUT, not_3_out, not_4_out, MAR_IN);
  not not_5 (not_5_out, DMA_REQ);
  ROM #(.addrWidth(10), .dataWidth(16)) rom_1 (.addr({INST, UC, FLAGS_OUT}), .data(rom_1_data));  // open: sel
  _16_nor u_16_nor_1 (.Input(rom_1_data), .Output(n16_nor_1_output));
  Counter #(.width(3), .max('h7), .trigger("falling")) Micro_counter (
    .count(pull_resistor_2_node), .Q(UC), .clk(CLK), .clr(UC_RESET));  // open: load, D, carry
  Pull_Resistor pull_resistor_2 (.node(pull_resistor_2_node));
  assign pull_resistor_2_node = not_5_out ? 1'b1 : 1'bz;  // Controlled_Buffer controlled_buffer_3
  assign UC_RESET = n16_nor_1_output ? 1'b1 : 1'bz;  // Controlled_Buffer controlled_buffer_4
  Register MAR (.D(BUS), .en(MAR_IN), .Q(MAR_q), .clk(CLK), .clr(FLAGS_RESET));
  Register #(.width(5)) IR (.D(BUS[4:0]), .en(IR_IN), .Q(INST), .clk(CLK), .clr(FLAGS_RESET));
  Button button_1 (.out(button_1_out));
  Button button_2 (.out(button_2_out));
  Button button_3 (.out(button_3_out));
  Button button_4 (.out(button_4_out));
  not not_6 (not_6_out, DMA_REQ);
  Pull_Resistor pull_resistor_3 (.node(pull_resistor_3_node));
  assign pull_resistor_3_node = not_6_out ? PC_INC : 1'bz;  // Controlled_Buffer controlled_buffer_5
  _7_Segment_Display u_7_segment_display_1 (
    .g(display_1_out_2[0]), .f(display_1_out_2[1]), .a(display_1_out_2[2]), .b(display_1_out_2[3]),
    .e(display_1_out_2_2[3]), .d(display_1_out_2_2[2]), .c(display_1_out_2_2[1]), .dp(display_1_out_2_2[0]));
  S_R_Flip_Flop #(.trigger("falling")) s_r_ff_1 (
    .S(button_1_out), .clk(PCLK), .R(button_2_out), .Q(s_r_ff_1_q));  // open: Qn, preset, reset, en
  or or_1 (or_1_out, button_2_out, button_4_out);
  assign controlled_buffer_6_out = RAM_IN ? BUS : 8'bz;  // Controlled_Buffer controlled_buffer_6
  RAM ram_1 (.addr(MAR_q), .data(controlled_buffer_6_out), .sel(1'b1), .clk(CLK), .ld(not_7_out));  // open: clr
  not not_7 (not_7_out, RAM_IN);
  Counter PC (
    .load(PC_IN), .D(BUS), .count(pull_resistor_3_node), .Q(PC_q), .clk(CLK), .clr(FLAGS_RESET));  // open: carry
  _7_Segment_Display u_7_segment_display_2 (
    .g(display_1_out_3[0]), .f(display_1_out_3[1]), .a(display_1_out_3[2]), .b(display_1_out_3[3]),
    .e(display_1_out_3_2[3]), .d(display_1_out_3_2[2]), .c(display_1_out_3_2[1]), .dp(display_1_out_3_2[0]));
  assign DMA_REQ = s_r_ff_1_q ? 1'b1 : 1'bz;  // Controlled_Buffer controlled_buffer_7
  LED led_17 (.in(s_r_ff_1_q));
  S_R_Flip_Flop #(.trigger("falling")) s_r_ff_2 (
    .S(or_1_out), .clk(PCLK), .R(FLAGS_RESET), .Q(FLAGS_RESET));  // open: Qn, preset, reset, en
  assign UC_RESET = FLAGS_RESET ? 1'b1 : 1'bz;  // Controlled_Buffer controlled_buffer_8
  DotMatrix #(.matrixcols(8), .matrixrows(1)) dotmatrix_1 (
    .col0(BUS[7]), .col1(BUS[6]), .col2(BUS[5]), .col3(BUS[4]), .col4(BUS[3]), .col5(BUS[2]), .col6(BUS[1]),
    .col7(BUS[0]));
  assign BUS = RAM_OUT ? controlled_buffer_6_out : 8'bz;  // Controlled_Buffer controlled_buffer_9
  assign BUS = PC_OUT ? PC_q : 8'bz;  // Controlled_Buffer controlled_buffer_10
  display display_1 (
    .in_1(OUTPUT_DATA), .out_2({display_1_out_2_2, display_1_out_2}),
    .out_3({display_1_out_3_2, display_1_out_3}), .out_4(display_1_out_4));
  _7_Segment_Display u_7_segment_display_3 (
    .g(display_1_out_4[0]), .f(display_1_out_4[1]), .a(display_1_out_4[2]), .b(display_1_out_4[3]),
    .e(display_1_out_4[7]), .d(display_1_out_4[6]), .c(display_1_out_4[5]), .dp(display_1_out_4[4]));
  Clock clock_2 (.out(clock_2_out));
  Pull_Resistor pull_resistor_4 (.node(DMA_REQ));
  Pull_Resistor pull_resistor_5 (.node(UC_RESET));
  Pull_Resistor pull_resistor_6 (.node(BUS));
  Counter #(.width(1), .max('h1)) counter_1 (
    .count(1'b1), .Q(counter_1_q), .clk(LEDS_OUT));  // open: load, D, carry, clr
  programmer programmer_1 (
    .Program_memory_address_select(MAR_IN), .Programming_enabled(programmer_1_programming_enabled),
    .Clock(PCLK), .DMA_request_enabled(s_r_ff_1_q), .Toggle_programming(button_3_out),
    .Program_select(register_1_q), .Bus_output(BUS), .Program_memory_data_select(RAM_IN));
  Register #(.width(4)) register_1 (.Q(register_1_q));  // open: D, en, clk, clr
  Adder adder_1 (
    .a(8'hdf), .b(counter_2_q), .out({adder_1_out[7:5], adder_1_out_2, adder_1_out[0]}), .cout(adder_1_cout));  // open: cin
  Counter #(.max('h80), .ongoal("stay")) counter_2 (
    .count(t_ff_1_q), .Q(counter_2_q), .clk(t_ff_2_q), .clr(t_ff_1_qn));  // open: load, D, carry
  assign controlled_buffer_11_out = t_ff_1_q ? clock_2_out : 1'bz;  // Controlled_Buffer controlled_buffer_11
  assign DMA_REQ = t_ff_1_q ? 1'b1 : 1'bz;  // Controlled_Buffer controlled_buffer_12
  T_Flip_Flop t_ff_1 (
    .clk(counter_1_q), .T(1'b1), .Q(t_ff_1_q), .Qn(t_ff_1_qn), .reset(adder_1_cout), .en(1'b1));  // open: preset
  LED led_18 (.in(programmer_1_programming_enabled));
  assign BUS = RA_OUT ? RA : 8'bz;  // Controlled_Buffer controlled_buffer_13
  Register u_RA (.D(BUS), .en(RA_IN), .Q(RA), .clk(CLK));  // open: clr
  Register u_RB (.D(BUS), .en(RB_IN), .Q(RB), .clk(CLK));  // open: clr
  Register u_OUTPUT (.D(BUS), .en(OUTPUT), .Q(OUTPUT_DATA), .clk(CLK));  // open: clr
  assign BUS = t_ff_2_q ? {adder_1_out[7:5], adder_1_out_2, adder_1_out[0]} : 8'bz;  // Controlled_Buffer controlled_buffer_14
  T_Flip_Flop t_ff_2 (
    .clk(controlled_buffer_11_out), .T(1'b1), .Q(t_ff_2_q), .Qn(t_ff_2_qn), .reset(adder_1_cout), .en(1'b1));  // open: preset
  assign MAR_IN = and_3_out ? 1'b1 : 1'bz;  // Controlled_Buffer controlled_buffer_15
  and and_2 (and_2_out, t_ff_2_qn, DMA_REQ);
  Register #(.width(4)) register_2 (.D(adder_1_out_2), .en(1'b1), .Q(register_2_q), .clk(t_ff_3_q));  // open: clr
  and and_3 (and_3_out, t_ff_2_q, t_ff_1_q);
  assign RAM_OUT = and_2_out ? 1'b1 : 1'bz;  // Controlled_Buffer controlled_buffer_16
  Hex_Digit_Display hex_digit_display_1 (.value(SUM[7:4]));  // open: dp
  Hex_Digit_Display hex_digit_display_2 (.value(SUM[3:0]));  // open: dp
  TTY tty_1 (.data(BUS[6:0]), .clk(CLK), .we(AOUT));  // open: clr
  Demultiplexer #(.width(8)) demultiplexer_1 (
    .out0(demultiplexer_1_out0), .out1(demultiplexer_1_out1), .in(BUS), .sel(t_ff_3_q), .en(1'b1));
  T_Flip_Flop t_ff_3 (
    .clk(controlled_buffer_11_out), .T(and_2_out), .Q(t_ff_3_q), .Qn(t_ff_3_qn), .en(1'b1));  // open: preset, reset
  DotMatrix #(.matrixcols(16), .matrixrows(16)) dotmatrix_2 (
    .col0(demultiplexer_2_out0), .col1(demultiplexer_2_out1), .col2(demultiplexer_2_out2),
    .col3(demultiplexer_2_out3), .col4(demultiplexer_2_out4), .col5(demultiplexer_2_out5),
    .col6(demultiplexer_2_out6), .col7(demultiplexer_2_out7), .col8(demultiplexer_2_out8),
    .col9(demultiplexer_2_out9), .col10(demultiplexer_2_out10), .col11(demultiplexer_2_out11),
    .col12(demultiplexer_2_out12), .col13(demultiplexer_2_out13), .col14(demultiplexer_2_out14),
    .col15(demultiplexer_2_out15));
  Demultiplexer #(.select(4), .width(16)) demultiplexer_2 (
    .out0(demultiplexer_2_out0), .out1(demultiplexer_2_out1), .out2(demultiplexer_2_out2),
    .out3(demultiplexer_2_out3), .out4(demultiplexer_2_out4), .out5(demultiplexer_2_out5),
    .out6(demultiplexer_2_out6), .out7(demultiplexer_2_out7), .out8(demultiplexer_2_out8),
    .out9(demultiplexer_2_out9), .out10(demultiplexer_2_out10), .out11(demultiplexer_2_out11),
    .out12(demultiplexer_2_out12), .out13(demultiplexer_2_out13), .out14(demultiplexer_2_out14),
    .out15(demultiplexer_2_out15), .in({register_3_q, register_4_q}), .sel(register_2_q), .en(1'b1));
  Register register_3 (.D(demultiplexer_1_out1), .en(1'b1), .Q(register_3_q), .clk(t_ff_3_qn));  // open: clr
  Register register_4 (.D(demultiplexer_1_out0), .en(1'b1), .Q(register_4_q), .clk(t_ff_3_q));  // open: clr
  inverter inverter_1 (.\output (inverter_1_output), .\input (RB), .enable(SUB));
  xor xor_1 (n16_nor_2_output[1], SUB, adder_2_cout);
  Adder adder_2 (.a(RA), .b(inverter_1_output), .out(SUM), .cin(SUB), .cout(adder_2_cout));
  assign BUS = ALU_OUT ? SUM : 8'bz;  // Controlled_Buffer controlled_buffer_17
  Register #(.width(2)) register_5 (.D(n16_nor_2_output), .en(ALU_OUT), .Q(FLAGS_OUT), .clk(CLK), .clr(FLAGS_RESET));
  _16_nor u_16_nor_2 (.Input({{8{1'b0}}, SUM}), .Output(n16_nor_2_output[0]));

  // Other names for the same wires on the sheet: IR_RESET = FLAGS_RESET; MAR_RESET = FLAGS_RESET;
  //   PC_RESET = FLAGS_RESET; PMAR_RESET = FLAGS_RESET

  // Notes on the sheet:
  //   Instructions ROM
  //   contents of rom_1 (hex, n*v repeats v):
  //   4*11 4*42 24*800 4*11 4*42 4*10 4*a 16*800 4*11 4*42 4*10 4*12 4*a 12*800 4*11 4*42 11 11 10 10 800
  //   800 a a 16*800 4*11 4*42 4*10 4*82 4*801 12*800 4*11 4*42 4*10 4*12 4*82 4*801 8*800 4*11 4*42 4*104
  //   20*800 4*11 4*42 4*10 4*202 4*801 12*800 4*11 4*42 4*10 4*6 4*801 12*800 4*11 4*42 4*10 4*12 4*6
  //   4*801 8*800 4*11 4*42 4*10 4*203 4*480 12*800 4*11 4*42 4*10 4*12 4*202 4*480 4*801 4*800 4*11 4*42
  //   4*10 4*4203 4*4480 12*800 4*11 4*42 4*10 4*12 4*4202 4*4480 4*801 4*800 4*11 4*42 4*10 4*12 4*2100
  //   4*801 8*800 4*11 4*42 11 10 11 10 800 a 800 a 16*800 4*11 4*42 4*11 20*800 4*11 4*42 4*11 20*800
  //   4*11 4*42 4*10 4*12 4*202 4*801 8*800 4*11 4*42 4*20 20*800 4*11 4*42 4*800 20*0 4*11 4*42 4*800
  //   20*0 4*11 4*42 4*800 20*0 4*11 4*42 4*800 20*0 4*11 4*42 4*800 20*0 4*11 4*42 4*800 20*0 4*11 4*42
  //   4*800 20*0 4*11 4*42 4*800 20*0 4*11 4*42 4*800 20*0 4*11 4*42 4*800 20*0 4*11 4*42 4*800 20*0 4*11
  //   4*42 4*1000 19*800
  //   Highr 3 bits ignored
  //   RAM
  //   ALU
endmodule

// 16 bit NOR
module _16_nor (
  input  [15:0] Input,
  output Output
);

  nor nor_1 (Output, Input[0], Input[1], Input[2], Input[3], Input[4], Input[5], Input[6], Input[7], Input[8], Input[9], Input[10], Input[11], Input[12], Input[13], Input[14], Input[15]);

  // Notes on the sheet:
  //   Input: pull=down
endmodule

module programmer (
  input  Clock,
  input  DMA_request_enabled,
  input  Toggle_programming,
  input  [3:0] Program_select,
  output Program_memory_address_select,
  output Programming_enabled,
  output [7:0] Bus_output,
  output Program_memory_data_select
);

  wire and_1_out, and_3_out, and_4_out, counter_1_q, counter_2_q, not_1_out, or_1_out, register_1_q;
  wire [7:0] counter_3_q, rom_1_data;

  Clock clock_1 ();  // open: out
  Button button_1 ();  // open: out
  or or_1 (or_1_out, Toggle_programming, register_1_q);
  assign Program_memory_address_select = and_1_out ? 1'b1 : 1'bz;  // Controlled_Buffer controlled_buffer_1
  and and_1 (and_1_out, DMA_request_enabled, not_1_out);
  Counter #(.width(1), .max('h1), .trigger("falling")) counter_1 (
    .count(Programming_enabled), .Q(counter_1_q), .clk(Clock), .clr(or_1_out));  // open: load, D, carry
  and and_2 (Programming_enabled, DMA_request_enabled, counter_2_q);
  Counter #(.width(1), .max('h1)) counter_2 (
    .count(or_1_out), .Q(counter_2_q), .clk(or_1_out));  // open: load, D, carry, clr
  not not_1 (not_1_out, counter_1_q);
  Counter #(.trigger("falling")) counter_3 (
    .count(counter_2_q), .Q(counter_3_q), .clk(counter_1_q), .clr(or_1_out));  // open: load, D, carry
  and and_3 (and_3_out, counter_1_q, DMA_request_enabled);
  assign Bus_output = and_1_out ? counter_3_q : 8'bz;  // Controlled_Buffer controlled_buffer_2
  ROM #(.addrWidth(12)) rom_1 (.addr({Program_select, counter_3_q}), .data(rom_1_data), .sel(and_3_out));
  assign Program_memory_data_select = Programming_enabled ? and_3_out : 1'bz;  // Controlled_Buffer controlled_buffer_3
  Register #(.width(1), .trigger("falling")) register_1 (
    .D(and_4_out), .en(and_4_out), .Q(register_1_q), .clk(counter_1_q), .clr(or_1_out));
  and and_4 (and_4_out, and_3_out, counter_1_q, counter_3_q[0], counter_3_q[1], counter_3_q[2], counter_3_q[3], counter_3_q[4], counter_3_q[5], counter_3_q[6], counter_3_q[7], counter_3_q[7]);
  assign Bus_output = Programming_enabled ? rom_1_data : 8'bz;  // Controlled_Buffer controlled_buffer_4

  // Notes on the sheet:
  //   Program_memory_data_select: pull=down
  //   Program_memory_address_select: pull=down
  //   Programming_enabled: pull=up
  //   DMA_request_enabled: pull=down
  //   Programs ROM
  //   contents of rom_1 (hex, n*v repeats v):
  //   5 ff e fd 6 5 fe c 1 e fa 5 ff c 1 e fc 5 fc e fb 5 fd b ff e fd 5 fb c 1 e fb 5 fd f 27 1 15 6 e ff
  //   5 fa c 1 e fa f 34 1 11 1f 201*0 5 3 5 fd d fe f 13 3 19 e fd 5 ff a 1 e ff 6 1 0 5 ff a 1 6 1f 5 ff
  //   6 1f 224*0 70 1b 0 5 fe b ff 3 12 6 e ff b fe 3 12 6 e fe 1 2 1f 235*0 1 0 4 a 6 c 1 6 f a 1 3 1f
  //   245*0 5 fe c 1 e ff 5 fe 6 d ff e fe 3 17 f 13 1 6 5 ff 6 1f 5 fd e fe 5 ff c 1 6 e ff 1 6 217*0 f 5
  //   0 5 fe c 1 e ff 5 fe 6 f 13 d ff e fe 3 17 1 6 5 ff 6 1f 5 fd e fe 5 ff c 1 6 e ff 1 6 217*0 b b
endmodule

module inverter (
  input  enable,
  input  [7:0] \input ,
  output [7:0] \output 
);

  xor xor_1 (\output [7], \input [7], enable);
  xor xor_2 (\output [6], \input [6], enable);
  xor xor_3 (\output [5], \input [5], enable);
  xor xor_4 (\output [4], \input [4], enable);
  xor xor_5 (\output [3], \input [3], enable);
  xor xor_6 (\output [1], \input [1], enable);
  xor xor_7 (\output [2], \input [2], enable);
  xor xor_8 (\output [0], \input [0], enable);

  // Notes on the sheet:
  //   input: pull=down
endmodule

module display (
  input  [7:0] in_1,
  output [7:0] out_2,
  output [7:0] out_3,
  output [7:0] out_4
);

  wire clock_1_out, n8_bit_or_1_output, n8_bit_or_2_output, n8_bit_or_3_output;
  wire [1:0] counter_1_q;
  wire [7:0] demultiplexer_1_out0, demultiplexer_1_out1, demultiplexer_1_out2, rom_1_data;

  DotMatrix #(.matrixcols(2), .matrixrows(1)) dotmatrix_1 (.col0(counter_1_q[1]), .col1(counter_1_q[0]));
  Counter #(.width(2), .max('h3)) counter_1 (.Q(counter_1_q), .clk(clock_1_out));  // open: load, D, count, carry, clr
  Clock clock_1 (.out(clock_1_out));
  DotMatrix #(.matrixcols(10), .matrixrows(1)) dotmatrix_2 (
    .col0(counter_1_q[1]), .col1(counter_1_q[0]), .col2(in_1[7]), .col3(in_1[6]), .col4(in_1[5]),
    .col5(in_1[4]), .col6(in_1[3]), .col7(in_1[2]), .col8(in_1[1]), .col9(in_1[0]));
  _8_bit_or u_8_bit_or_1 (.\input (demultiplexer_1_out2), .Output(n8_bit_or_1_output));
  Register register_1 (.D(demultiplexer_1_out2), .en(n8_bit_or_1_output), .Q(out_2), .clk(clock_1_out));  // open: clr
  ROM #(.addrWidth(10)) rom_1 (.addr({counter_1_q, in_1}), .data(rom_1_data));  // open: sel
  Demultiplexer #(.select(2), .width(8), .disabled(0), .enable("false")) demultiplexer_1 (
    .out0(demultiplexer_1_out0), .out1(demultiplexer_1_out1), .out2(demultiplexer_1_out2), .in(rom_1_data),
    .sel(counter_1_q));  // open: out3
  _8_bit_or u_8_bit_or_2 (.\input (demultiplexer_1_out1), .Output(n8_bit_or_2_output));
  Register register_2 (.D(demultiplexer_1_out1), .en(n8_bit_or_2_output), .Q(out_3), .clk(clock_1_out));  // open: clr
  _8_bit_or u_8_bit_or_3 (.\input (demultiplexer_1_out0), .Output(n8_bit_or_3_output));
  Register register_3 (.D(demultiplexer_1_out0), .en(n8_bit_or_3_output), .Q(out_4), .clk(clock_1_out));  // open: clr

  // Notes on the sheet:
  //   contents of rom_1 (hex, n*v repeats v):
  //   ee 28 cd 6d 2b 67 e7 2c ef 6f ee 28 cd 6d 2b 67 e7 2c ef 6f ee 28 cd 6d 2b 67 e7 2c ef 6f ee 28 cd
  //   6d 2b 67 e7 2c ef 6f ee 28 cd 6d 2b 67 e7 2c ef 6f ee 28 cd 6d 2b 67 e7 2c ef 6f ee 28 cd 6d 2b 67
  //   e7 2c ef 6f ee 28 cd 6d 2b 67 e7 2c ef 6f ee 28 cd 6d 2b 67 e7 2c ef 6f ee 28 cd 6d 2b 67 e7 2c ef
  //   6f ee 28 cd 6d 2b 67 e7 2c ef 6f ee 28 cd 6d 2b 67 e7 2c ef 6f ee 28 cd 6d 2b 67 e7 2c ef 6f ee 28
  //   cd 6d 2b 67 e7 2c ef 6f ee 28 cd 6d 2b 67 e7 2c ef 6f ee 28 cd 6d 2b 67 e7 2c ef 6f ee 28 cd 6d 2b
  //   67 e7 2c ef 6f ee 28 cd 6d 2b 67 e7 2c ef 6f ee 28 cd 6d 2b 67 e7 2c ef 6f ee 28 cd 6d 2b 67 e7 2c
  //   ef 6f ee 28 cd 6d 2b 67 e7 2c ef 6f ee 28 cd 6d 2b 67 e7 2c ef 6f ee 28 cd 6d 2b 67 e7 2c ef 6f ee
  //   28 cd 6d 2b 67 e7 2c ef 6f ee 28 cd 6d 2b 67 e7 2c ef 6f ee 28 cd 6d 2b 67 10*ee 10*28 10*cd 10*6d
  //   10*2b 10*67 10*e7 10*2c 10*ef 10*6f 10*ee 10*28 10*cd 10*6d 10*2b 10*67 10*e7 10*2c 10*ef 10*6f
  //   10*ee 10*28 10*cd 10*6d 10*2b 6*67 100*ee 100*28 56*cd
endmodule

module _8_bit_or (
  input  [7:0] \input ,
  output Output
);

  or or_1 (Output, \input [0], \input [1], \input [2], \input [3], \input [4], \input [5], \input [6], \input [7]);

  // Notes on the sheet:
  //   input: pull=down
  //   Output: pull=down
endmodule
