// Logisim project test2.circ as structural Verilog: 1 circuit, main circuit main
module main (
);

  wire clock_1_out, undriven;
  wire [7:0] ram_1_data, register_1_q, register_2_q;

  Clock clock_1 (.out(clock_1_out));
  Register register_1 (.D(ram_1_data), .en(undriven), .Q(register_1_q), .clk(clock_1_out));  // open: clr
  Register register_2 (.D(ram_1_data), .en(undriven), .Q(register_2_q), .clk(clock_1_out));  // open: clr
  ROM #(.addrWidth(16)) rom_1 ();  // open: addr, data, sel
  Decoder #(.select(3)) decoder_1 ();  // open: out0, out1, out2, out3, out4, out5, out6, out7, sel, en
  RAM #(.addrWidth(16)) ram_1 (
    .addr({register_2_q, register_1_q}), .data(ram_1_data), .clk(clock_1_out));  // open: sel, ld, clr

  // Notes on the sheet:
  //   ram address register
endmodule
